// Digital circuit lutcomp.dig as structural Verilog
module lutcomp (
  input  RESET
);

  wire ADDR_OE, not_1_out, pc_1_p2;
  wire [2:0] ALU_OP;
  wire [3:0] undriven;
  wire [7:0] uROM_d;
  wire [19:0] undriven_2;

  ROM #(.AddrBits(20), .Bits(8)) uROM (.A(undriven_2), .sel(1'b1), .D(uROM_d));
  // _74238 _74238_1: pin names not known
  // Probe on undriven_2
  // Probe on uROM_d
  // _74574 uIR1: pin names not known
  // _74574 uIR0: pin names not known; wires that end beside it: 1'b0, 1'b0, 1'b1
  not not_1 (not_1_out, ADDR_OE);
  // Probe on {ADDR_OE, ALU_OP, undriven}
  // pc pc_1: pin names not known; wires that end beside it: not_1_out, pc_1_p2
  // Probe on pc_1_p2
  // _74238 _74238_2: pin names not known
  // _74238 _74238_3: pin names not known
  // _74138 _74138_1: pin names not known; wires that end beside it: 1'b0, undriven[3], RESET, 1'b0, 1'b1
  // _74138 _74138_2: pin names not known; wires that end beside it: 1'b0, 1'b0, undriven[3], 1'b0, 1'b1

  // Notes on the sheet:
  //   uROM loads ucode.hex
  //   3A
  //   3Y
endmodule
